# Fritzing sketch ESP32-S2 Eletrical Squeeme (saved by Fritzing 0.9.3b)
breadboards: 1

parts:
  M1 = ESP32-S2-DevKitM-1 [part_number=ESP32-S2-DevKitM-1]
  DHT1 = Humidity and Temperature Sensor DHT11
  M2 = PH meter with sensor in breadboard [package=THT]
  R1 = Resistor [tolerance=±5% resistance=33k package=THT]
  R2 = Resistor [tolerance=±5% resistance=20k package=THT]

nets:
  N1: M1.G-21, M1.G-42, DHT1.GND_2, M2.pin3, R1.Pin_0
  3V3: M1.3V3, DHT1.Vcc, M2.pin2
  N2: M1.0, DHT1.Data-signal
  N3: M1.1, R1.Pin_1, R2.Pin_1
  N4: M2.pin1, R2.Pin_0

custom parts:
  ESP32-S2-DevKitM-1: The DOIT Esp32 DevKit v1 is one of the development board created by DOIT to evaluate the ESP-WROOM-32 module. It is based on the ESP32 microcontroller that boasts Wifi, Bluetooth, Ethernet and Low Power support all in a single chip. (vanepp) Feb 2021: converted to ESP32-S2-DevKitM-1. This module is 42pins long (2x21) and 11 pins width.
  Humidity and Temperature Sensor DHT11: Digital relative humidity & temperature sensor DHT11
  PH meter with sensor in breadboard: DFrobot PH meter (SKU SEN0161)
