# Fritzing sketch ESP32-S2 Eletrical Squeeme (saved by Fritzing 0.9.3b)
breadboards: 1

parts:
  M1 = ESP32-S2-DevKitM-1 [part_number=ESP32-S2-DevKitM-1]
  DHT1 = Humidity and Temperature Sensor DHT11
  R1 = Resistor [tolerance=±5% resistance=47k package=THT]
  R2 = Resistor [tolerance=±5% resistance=47k package=THT]
  M2 = PH meter with sensor in breadboard [package=THT]
  part = Water Level Sensor
  R3 = Resistor [tolerance=±5% resistance=47k package=THT]
  R4 = Resistor [tolerance=±5% resistance=47k package=THT]
  M3 = PH meter with sensor in breadboard [package=THT]

nets:
  N1: M1.G-21, M1.G-42, DHT1.GND_1, R1.Pin_0, R2.Pin_1, M2.pin3, part.GND, M3.pin3
  N2: M1.1, R2.Pin_0, R4.Pin_0
  N3: M1.2, R1.Pin_1, R3.Pin_0
  N4: M1.3, part.SIG
  N5: M1.9, DHT1.Data-signal
  VCC: M1.15, DHT1.Vcc, M2.pin2, part.VCC, M3.pin2
  N6: M2.pin1, R4.Pin_1
  N7: R3.Pin_1, M3.pin1

custom parts:
  ESP32-S2-DevKitM-1: The DOIT Esp32 DevKit v1 is one of the development board created by DOIT to evaluate the ESP-WROOM-32 module. It is based on the ESP32 microcontroller that boasts Wifi, Bluetooth, Ethernet and Low Power support all in a single chip. (vanepp) Feb 2021: converted to ESP32-S2-DevKitM-1. This module is 42pins long (2x21) and 11 pins width.
  Humidity and Temperature Sensor DHT11: Digital relative humidity & temperature sensor DHT11
  PH meter with sensor in breadboard: DFrobot PH meter (SKU SEN0161)
  Water Level Sensor: A water level sensor. This sensor operates at 3V to 5V. The Sig (signal) pin outputs an analogue signal that is in proportion to the amount of water in contact with the sensor.
