# Fritzing sketch ESP32-S2-Assembly (saved by Fritzing 0.9.3b)
breadboards: 1

parts:
  M1 = ESP32-S2-DevKitM-1 [part_number=ESP32-S2-DevKitM-1]
  DHT1 = Humidity and Temperature Sensor DHT11
  R1 = Resistor [tolerance=±5% resistance=47k package=THT]
  M2 = PH meter with sensor in breadboard [package=THT]
  Water_Level_Sensor = Water Level Sensor
  M3 = PH meter with sensor in breadboard [package=THT]
  R3 = Resistor [tolerance=±5% resistance=47k package=THT]
  R4 = Resistor [tolerance=±5% resistance=47k package=THT]
  Q1 = npn-Powertransistor [package="TO220 [THT]"]
  R2 = Resistor [tolerance=±5% resistance=47k package=THT]

nets:
  N1: M1.G-21, M1.G-42, DHT1.GND_2, R1.Pin_0, Water_Level_Sensor.GND, R4.Pin_0, Q1.emitter
  N2: M1.1, R1.Pin_1, R2.Pin_1
  N3: M1.2, R3.Pin_1, R4.Pin_1
  N4: M1.3, Water_Level_Sensor.SIG
  N5: M1.9, DHT1.Data-signal
  N6: M1.11, Water_Level_Sensor.VCC
  N7: M1.13, Q1.base
  N8: M1.15, DHT1.Vcc
  N9: M1.5V, M2.pin2, M3.pin2
  N10: M2.pin1, R2.Pin_0
  N11: M2.pin3, M3.pin3, Q1.collector
  N12: M3.pin1, R3.Pin_0

custom parts:
  ESP32-S2-DevKitM-1: The DOIT Esp32 DevKit v1 is one of the development board created by DOIT to evaluate the ESP-WROOM-32 module. It is based on the ESP32 microcontroller that boasts Wifi, Bluetooth, Ethernet and Low Power support all in a single chip. (vanepp) Feb 2021: converted to ESP32-S2-DevKitM-1. This module is 42pins long (2x21) and 11 pins width.
  Humidity and Temperature Sensor DHT11: Digital relative humidity & temperature sensor DHT11
  PH meter with sensor in breadboard: DFrobot PH meter (SKU SEN0161)
  Water Level Sensor: A water level sensor. This sensor operates at 3V to 5V. The Sig (signal) pin outputs an analogue signal that is in proportion to the amount of water in contact with the sensor.
